// Logisim project cpu.circ as structural Verilog: 4 circuits, main circuit main
module main (
);

  ALU_Aritmetica_16b alu_aritmetica_16b_1 ();  // open: A, B, SUB, Cout, S
endmodule

module ALU_FullAdder (
  input  Cin,
  input  A,
  input  B,
  output S,
  output Cout
);

  wire and_1_out, and_2_out, xor_1_out;

  and and_1 (and_1_out, A, B);
  xor xor_1 (xor_1_out, A, B);
  xor xor_2 (S, Cin, xor_1_out);
  and and_2 (and_2_out, Cin, xor_1_out);
  or or_1 (Cout, and_2_out, and_1_out);
endmodule

module ALU_Adder4 (
  input  Cin,
  input  [3:0] A,
  input  [3:0] B,
  output [3:0] S,
  output Cout
);

  wire alu_fulladder_1_cout, alu_fulladder_2_cout, alu_fulladder_3_cout;

  ALU_FullAdder alu_fulladder_1 (.Cin(Cin), .A(A[0]), .B(B[0]), .S(S[0]), .Cout(alu_fulladder_1_cout));
  ALU_FullAdder alu_fulladder_2 (.Cin(alu_fulladder_1_cout), .A(A[1]), .B(B[1]), .S(S[1]), .Cout(alu_fulladder_2_cout));
  ALU_FullAdder alu_fulladder_3 (.Cin(alu_fulladder_2_cout), .A(A[2]), .B(B[2]), .S(S[2]), .Cout(alu_fulladder_3_cout));
  ALU_FullAdder alu_fulladder_4 (.Cin(alu_fulladder_3_cout), .A(A[3]), .B(B[3]), .S(S[3]), .Cout(Cout));
endmodule

module ALU_Aritmetica_16b (
  input  [15:0] A,
  input  [15:0] B,
  input  SUB,
  output [15:0] S,
  output Cout
);

  wire alu_adder4_1_cout, alu_adder4_2_cout, alu_adder4_3_cout;
  wire [3:0] xor_1_out;
  wire [15:0] bit_extender_1_out;
  wire [15:4] xor_1_out_2;

  assign bit_extender_1_out = {{15{SUB}}, SUB};  // Bit_Extender bit_extender_1
  assign {xor_1_out_2, xor_1_out} = B ^ bit_extender_1_out;  // XOR_Gate xor_1, 16 bits wide
  ALU_Adder4 alu_adder4_1 (.Cin(SUB), .A(A[3:0]), .B(xor_1_out), .S(S[3:0]), .Cout(alu_adder4_1_cout));
  ALU_Adder4 alu_adder4_2 (
    .Cin(alu_adder4_1_cout), .A(A[7:4]), .B(xor_1_out_2[7:4]), .S(S[7:4]), .Cout(alu_adder4_2_cout));
  ALU_Adder4 alu_adder4_3 (
    .Cin(alu_adder4_2_cout), .A(A[11:8]), .B(xor_1_out_2[11:8]), .S(S[11:8]), .Cout(alu_adder4_3_cout));
  ALU_Adder4 alu_adder4_4 (.Cin(alu_adder4_3_cout), .A(A[15:12]), .B(xor_1_out_2[15:12]), .S(S[15:12]), .Cout(Cout));
endmodule
